# Fritzing sketch fartlek (saved by Fritzing 0.9.3b)

parts:
  Part1 = Adafruit Trinket 5V
  SG1 = Buzzer 12mm [package=buzzer-ccv-kit]
  S2 = Momentary Switch [package=ksa_sealed_tac_switch]
  U1 = LIPO-110mAh [package=lipo-110]

nets:
  N1: Part1.VBAT, S2.1
  N2: Part1.GND, SG1.1, U1.-
  N3: Part1.#1, SG1.2
  N4: S2.4, U1.+

custom parts:
  Adafruit Trinket 5V: Trinket may be small, but do not be fooled by its size! It's a tiny microcontroller board, built around the Atmel ATtiny85, a little chip with a lot of power. We wanted to design a microcontroller board that was small enough to fit into any project, and low cost enough to use without hesitation. Perfect for when you don't want to give up your expensive dev-board and you aren't willing to take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
